// Logisim project Ch7.circ as structural Verilog
module processor (
);

  wire AluInAClk, AluInBClk, AluOutClk, CarryInClk, Decode, InsRegClk, MemClk, MemInClk, MemOutClk,
       MemSelClk, RegClk, RegInClk, RegOutClk, RegSelClk;
  wire [1:0] InsRegSel, RegInpSel, register_1_q;
  wire [2:0] multiplexer_2_out, n16_bit_alu_2_1_out_6, register_1_q_2, register_1_q_3, register_1_q_4,
       register_3_q, register_6_q, register_7_q, register_11_q, register_15_q;
  wire [3:0] control_logic_1_microstep, register_2_q, register_8_q;
  wire [4:0] register_1_q_5;
  wire [4:4] register_2_q_2;
  wire [7:0] register_9_q;
  wire [15:0] carry_in_1_out, memory_1_data_out, multiplexer_1_out, n16_bit_alu_2_1_result, register_4_q,
       register_5_q, register_10_q, register_13_q, register_16_q, register_17_q, register_18_q,
       register_19_q, Registers_p2, Registers_p3, Registers_p4, Registers_p5, Registers_p8, Registers_p9,
       Registers_p10, Registers_p11, Registers_p12;

  Hex_Digit_Display hex_digit_display_1 (.value(control_logic_1_microstep));  // open: dp
  Control_Logic control_logic_1 (
    .Decode(Decode), .InsRegClk(InsRegClk), .AluInAClk(AluInAClk), .AluInBClk(AluInBClk),
    .AluOutClk(AluOutClk), .RegClk(RegClk), .RegSelClk(RegSelClk), .RegInClk(RegInClk),
    .RegOutClk(RegOutClk), .MemClk(MemClk), .MemSelClk(MemSelClk), .MemInClk(MemInClk),
    .MemOutClk(MemOutClk), .CarryInClk(CarryInClk), .RegInpSel(RegInpSel), .InsRegSel(InsRegSel),
    .OpCode({register_2_q_2[4], register_2_q}), .MicroStep(control_logic_1_microstep));
  Register #(.width(16), .trigger("high")) register_1 (
    .D(register_19_q), .Q({register_1_q_5, register_1_q_4, register_1_q_3, register_1_q_2, register_1_q}),
    .clk(InsRegClk));  // open: en, clr
  Register #(.width(5), .trigger("high")) register_2 (
    .D(register_1_q_5), .Q({register_2_q_2[4], register_2_q}), .clk(Decode));  // open: en, clr
  Register #(.width(3), .trigger("high")) register_3 (
    .D(register_1_q_4), .Q(register_3_q), .clk(Decode));  // open: en, clr
  Register #(.width(16), .trigger("high")) register_4 (
    .D(register_18_q), .Q(register_4_q), .clk(AluInAClk));  // open: en, clr
  Register #(.width(16), .trigger("high")) register_5 (
    .D(register_18_q), .Q(register_5_q), .clk(AluInBClk));  // open: en, clr
  Register #(.width(3), .trigger("high")) register_6 (
    .D(register_1_q_2), .Q(register_6_q), .clk(Decode));  // open: en, clr
  Register #(.width(3), .trigger("high")) register_7 (
    .D(register_1_q_3), .Q(register_7_q), .clk(Decode));  // open: en, clr
  Register #(.width(4), .trigger("high")) register_8 (
    .D(register_2_q), .Q(register_8_q), .clk(register_2_q_2[4]));  // open: en, clr
  Register #(.trigger("high")) register_9 (
    .D({register_1_q_3, register_1_q_2, register_1_q}), .Q(register_9_q), .clk(Decode));  // open: en, clr
  Register #(.width(16), .trigger("high")) register_10 (
    .D(n16_bit_alu_2_1_result), .Q(register_10_q), .clk(AluOutClk));  // open: en, clr
  _16_bit_alu_2 u_16_bit_alu_2_1 (
    .A(register_4_q), .B(register_5_q), .Result(n16_bit_alu_2_1_result), .in_1(register_8_q),
    .out_6(n16_bit_alu_2_1_out_6));  // open: CarryOut_Overflow
  Register #(.width(3), .trigger("high")) register_11 (
    .D(n16_bit_alu_2_1_out_6), .Q(register_11_q), .clk(register_2_q_2[4]));  // open: en, clr
  Multiplexer #(.select(2), .width(16), .enable("false")) multiplexer_1 (
    .in0({{8{1'b0}}, register_9_q}), .in1(register_19_q), .in2(register_10_q), .in3(carry_in_1_out),
    .out(multiplexer_1_out), .sel(RegInpSel));
  Carry_In carry_in_1 (.IN(register_18_q), .Out(carry_in_1_out), .Carry_In(CarryInClk));
  Register #(.width(16), .trigger("high")) register_12 (.D(carry_in_1_out), .clk(1'b1));  // open: en, Q, clr
  Multiplexer #(.select(2), .width(3), .enable("false")) multiplexer_2 (
    .in0(register_3_q), .in1(register_7_q), .in2(register_6_q), .in3(3'b000), .out(multiplexer_2_out),
    .sel(InsRegSel));
  // Probe on multiplexer_2_out
  Register #(.width(16), .trigger("high")) register_13 (
    .D(multiplexer_1_out), .Q(register_13_q), .clk(RegInClk));  // open: en, clr
  Register #(.width(16), .trigger("high")) register_14 (.D(register_18_q), .clk(1'b1));  // open: en, Q, clr
  Register #(.width(3), .trigger("high")) register_15 (
    .D(multiplexer_2_out), .Q(register_15_q), .clk(RegSelClk));  // open: en, clr
  // _16_bit_8_word_register Registers: pin names not known; wires that end beside it: register_13_q, Registers_p2, Registers_p3, Registers_p4, Registers_p5, register_15_q, RegClk, Registers_p8, Registers_p9, Registers_p10, Registers_p11, Registers_p12
  Register #(.width(16), .trigger("high")) register_16 (
    .D(register_18_q), .Q(register_16_q), .clk(MemSelClk));  // open: en, clr
  Register #(.width(16), .trigger("high")) register_17 (
    .D(register_18_q), .Q(register_17_q), .clk(MemInClk));  // open: en, clr
  Memory memory_1 (
    .Data_In(register_17_q), .Data_Out(memory_1_data_out), .Memory_Address(register_16_q), .Clock(MemClk));  // open: CLEAR
  Register #(.width(16), .trigger("high")) register_18 (
    .D(Registers_p11), .Q(register_18_q), .clk(RegOutClk));  // open: en, clr
  Register #(.width(16), .trigger("high")) register_19 (
    .D(memory_1_data_out), .Q(register_19_q), .clk(MemOutClk));  // open: en, clr
  Register #(.width(16), .trigger("high")) register_20 (.D(Registers_p12), .clk(1'b1));  // open: en, Q, clr
  Register #(.width(16), .trigger("high")) register_21 (.D(Registers_p10), .clk(1'b1));  // open: en, Q, clr
  Register #(.width(16), .trigger("high")) register_22 (.D(Registers_p9), .clk(1'b1));  // open: en, Q, clr
  Register #(.width(16), .trigger("high")) register_23 (.D(Registers_p8), .clk(1'b1));  // open: en, Q, clr
  Register #(.width(16), .trigger("high")) register_24 (.D(Registers_p5), .clk(1'b1));  // open: en, Q, clr
  Register #(.width(16), .trigger("high")) register_25 (.D(Registers_p4), .clk(1'b1));  // open: en, Q, clr
  Register #(.width(16), .trigger("high")) register_26 (.D(Registers_p3), .clk(1'b1));  // open: en, Q, clr
  Register #(.width(16), .trigger("high")) register_27 (.D(Registers_p2), .clk(1'b1));  // open: en, Q, clr
endmodule

module Control_Logic (
  input  [4:0] OpCode,
  output [3:0] MicroStep,
  output [1:0] InsRegSel,
  output MemClk,
  output MemInClk,
  output RegSelClk,
  output RegOutClk,
  output MemOutClk,
  output MemSelClk,
  output CarryInClk,
  output RegInClk,
  output [1:0] RegInpSel,
  output AluInAClk,
  output AluInBClk,
  output AluOutClk,
  output RegClk,
  output InsRegClk,
  output Decode
);

  wire and_1_out, and_2_out, clock_1_out, not_1_out, not_2_out;
  wire [3:0] demultiplexer_1_out0;
  wire [9:0] demultiplexer_1_out6, demultiplexer_2_out0, demultiplexer_2_out1, demultiplexer_3_out0,
       demultiplexer_3_out1, demultiplexer_3_out2, demultiplexer_3_out3;

  and and_1 (and_1_out, OpCode[4], OpCode[3], OpCode[2], OpCode[1], OpCode[0]);
  Pull_Resistor pull_resistor_1 (.node(and_1_out));
  Clock clock_1 (.out(clock_1_out));
  Hex_Digit_Display hex_digit_display_1 (.value(MicroStep));  // open: dp
  not not_1 (not_1_out, and_1_out);
  and and_2 (and_2_out, not_1_out, clock_1_out);
  hex_counter hex_counter_1 (.Clock_in(and_2_out), .Out(MicroStep));
  Demultiplexer #(.select(4), .enable("false")) demultiplexer_1 (
    .out0(demultiplexer_1_out0[0]), .out1(demultiplexer_1_out0[1]), .out2(CarryInClk),
    .out3(demultiplexer_1_out0[3]), .out4(InsRegClk), .out5(Decode), .out6(demultiplexer_1_out6[0]),
    .out7(demultiplexer_1_out6[1]), .out8(demultiplexer_1_out6[2]), .out9(demultiplexer_1_out6[3]),
    .out10(demultiplexer_1_out6[4]), .out11(demultiplexer_1_out6[5]), .out12(demultiplexer_1_out6[6]),
    .out13(demultiplexer_1_out6[7]), .out14(demultiplexer_1_out6[8]), .out15(demultiplexer_1_out6[9]),
    .in(1'b1), .sel(MicroStep));
  Demultiplexer #(.width(10), .disabled(0), .enable("false")) demultiplexer_2 (
    .out0({demultiplexer_2_out0[9:7], AluOutClk, AluInBClk, demultiplexer_2_out0[4:3], AluInAClk, demultiplexer_2_out0[1:0]}),
    .out1(demultiplexer_2_out1), .in(demultiplexer_1_out6), .sel(not_2_out));
  not not_2 (not_2_out, OpCode[4]);
  Demultiplexer #(.select(2), .width(10), .enable("false")) demultiplexer_3 (
    .out0(demultiplexer_3_out0), .out1(demultiplexer_3_out1), .out2(demultiplexer_3_out2),
    .out3(demultiplexer_3_out3), .in(demultiplexer_2_out1), .sel(OpCode[1:0]));
  Selector selector_1 (
    ._00(demultiplexer_2_out0[0]), ._01(demultiplexer_2_out0[3]), ._10(AluOutClk),
    ._11(demultiplexer_1_out0[0]), .X_(InsRegSel));
  or or_1 (RegOutClk, demultiplexer_1_out0[1], demultiplexer_2_out0[1], demultiplexer_2_out0[4]);
  Selector selector_2 (._10(demultiplexer_2_out0[7]), ._11(CarryInClk), .X_(RegInpSel));  // open: _00, _01
  or or_2 (RegSelClk, demultiplexer_1_out0[0], AluOutClk, demultiplexer_2_out0[3], demultiplexer_2_out0[0]);
  or or_3 (RegInClk, demultiplexer_2_out0[7], CarryInClk);
  or or_4 (RegClk, demultiplexer_2_out0[8], demultiplexer_1_out0[3]);

  assign MemOutClk = CarryInClk;
  assign MemSelClk = CarryInClk;

  // Notes on the sheet:
  //   CarryInClk: pull=down
  //   MemClk: pull=down
  //   Decode: pull=down
  //   AluOutClk: pull=down
  //   RegInClk: pull=down
  //   MemInClk: pull=down
  //   RegClk: pull=down
  //   RegOutClk: pull=down
  //   MemSelClk: pull=down
  //   InsRegClk: pull=down
  //   MemOutClk: pull=down
  //   AluInAClk: pull=down
  //   AluInBClk: pull=down
  //   RegSelClk: pull=down
endmodule

// 3
module _3_bit_register (
  input  Clock,
  input  [2:0] Input,
  input  Clock_2,
  output [2:0] Output
);

  D_Flip_Flop d_ff_1 (.clk(Clock), .D(Input[0]), .Q(Output[0]));  // open: Qn, preset, en, reset
  D_Flip_Flop d_ff_2 (.clk(Clock), .D(Input[1]), .Q(Output[1]));  // open: Qn, preset, en, reset
  D_Flip_Flop d_ff_3 (.clk(Clock), .D(Input[2]), .Q(Output[2]));  // open: Qn, preset, en, reset

  assign Clock_2 = Clock;
endmodule

// 5
module _5_bit_register (
  input  Clock,
  input  [4:0] Input,
  input  Clock_2,
  output [4:0] Output
);

  D_Flip_Flop d_ff_1 (.clk(Clock), .D(Input[0]), .Q(Output[0]));  // open: Qn, preset, en, reset
  D_Flip_Flop d_ff_2 (.clk(Clock), .D(Input[1]), .Q(Output[1]));  // open: Qn, preset, en, reset
  D_Flip_Flop d_ff_3 (.clk(Clock), .D(Input[2]), .Q(Output[2]));  // open: Qn, preset, en, reset
  D_Flip_Flop d_ff_4 (.clk(Clock), .D(Input[3]), .Q(Output[3]));  // open: Qn, preset, en, reset
  D_Flip_Flop d_ff_5 (.clk(Clock), .D(Input[4]), .Q(Output[4]));  // open: Qn, preset, en, reset

  assign Clock_2 = Clock;

  // Notes on the sheet:
  //   Input: pull=down
endmodule

// 8
module _8_bit_register (
  input  Clock,
  input  [7:0] Input,
  input  Clock_2,
  output [7:0] Output
);

  D_Flip_Flop d_ff_1 (.clk(Clock), .D(Input[0]), .Q(Output[0]));  // open: Qn, preset, en, reset
  D_Flip_Flop d_ff_2 (.clk(Clock), .D(Input[1]), .Q(Output[1]));  // open: Qn, preset, en, reset
  D_Flip_Flop d_ff_3 (.clk(Clock), .D(Input[2]), .Q(Output[2]));  // open: Qn, preset, en, reset
  D_Flip_Flop d_ff_4 (.clk(Clock), .D(Input[3]), .Q(Output[3]));  // open: Qn, preset, en, reset
  D_Flip_Flop d_ff_5 (.clk(Clock), .D(Input[4]), .Q(Output[4]));  // open: Qn, preset, en, reset
  D_Flip_Flop d_ff_6 (.clk(Clock), .D(Input[5]), .Q(Output[5]));  // open: Qn, preset, en, reset
  D_Flip_Flop d_ff_7 (.clk(Clock), .D(Input[6]), .Q(Output[6]));  // open: Qn, preset, en, reset
  D_Flip_Flop d_ff_8 (.clk(Clock), .D(Input[7]), .Q(Output[7]));  // open: Qn, preset, en, reset

  assign Clock_2 = Clock;
endmodule

// 16
module _16_bit_register (
  input  Clock,
  input  [15:0] Input,
  input  Clock_2,
  output [15:0] Output
);

  D_Flip_Flop d_ff_1 (.clk(Clock), .D(Input[14]), .Q(Output[14]));  // open: Qn, preset, en, reset
  D_Flip_Flop d_ff_2 (.clk(Clock), .D(Input[6]), .Q(Output[6]));  // open: Qn, preset, en, reset
  D_Flip_Flop d_ff_3 (.clk(Clock), .D(Input[8]), .Q(Output[8]));  // open: Qn, preset, en, reset
  D_Flip_Flop d_ff_4 (.clk(Clock), .D(Input[10]), .Q(Output[10]));  // open: Qn, preset, en, reset
  D_Flip_Flop d_ff_5 (.clk(Clock), .D(Input[12]), .Q(Output[12]));  // open: Qn, preset, en, reset
  D_Flip_Flop d_ff_6 (.clk(Clock), .D(Input[13]), .Q(Output[13]));  // open: Qn, preset, en, reset
  D_Flip_Flop d_ff_7 (.clk(Clock), .D(Input[15]), .Q(Output[15]));  // open: Qn, preset, en, reset
  D_Flip_Flop d_ff_8 (.clk(Clock), .D(Input[0]), .Q(Output[0]));  // open: Qn, preset, en, reset
  D_Flip_Flop d_ff_9 (.clk(Clock), .D(Input[2]), .Q(Output[2]));  // open: Qn, preset, en, reset
  D_Flip_Flop d_ff_10 (.clk(Clock), .D(Input[4]), .Q(Output[4]));  // open: Qn, preset, en, reset
  D_Flip_Flop d_ff_11 (.clk(Clock), .D(Input[5]), .Q(Output[5]));  // open: Qn, preset, en, reset
  D_Flip_Flop d_ff_12 (.clk(Clock), .D(Input[7]), .Q(Output[7]));  // open: Qn, preset, en, reset
  D_Flip_Flop d_ff_13 (.clk(Clock), .D(Input[9]), .Q(Output[9]));  // open: Qn, preset, en, reset
  D_Flip_Flop d_ff_14 (.clk(Clock), .D(Input[11]), .Q(Output[11]));  // open: Qn, preset, en, reset
  D_Flip_Flop d_ff_15 (.clk(Clock), .D(Input[1]), .Q(Output[1]));  // open: Qn, preset, en, reset
  D_Flip_Flop d_ff_16 (.clk(Clock), .D(Input[3]), .Q(Output[3]));  // open: Qn, preset, en, reset

  assign Clock_2 = Clock;
endmodule

module Instruction_Register (
  input  Decode,
  input  [15:0] In,
  input  Clock,
  output [15:0] Out
);

  Register #(.width(16), .trigger("high")) register_1 (.D(In), .clk(Clock));  // open: en, Q, clr

  assign Out = 16'h994c;
endmodule

module Carry_In (
  input  Carry_In,
  input  [15:0] IN,
  output [15:0] Out
);

  Adder #(.width(16)) adder_1 (.a(IN), .b({16{1'b0}}), .out(Out), .cin(Carry_In));  // open: cout

  // Notes on the sheet:
  //   Out: pull=down
endmodule

module Memory (
  input  CLEAR,
  input  [15:0] Memory_Address,
  input  [15:0] Data_In,
  input  Clock,
  output [15:0] Data_Out
);

  RAM #(.addrWidth(16), .dataWidth(16), .bus("separate")) ram_1 (
    .addr(Memory_Address), .din(Data_In), .data(Data_Out), .str(1'b1), .sel(1'b1), .clk(Clock), .ld(1'b1),
    .clr(CLEAR));

  // Notes on the sheet:
  //   Data_Out: pull=down
endmodule

module Selector (
  input  _00,
  input  _01,
  input  _10,
  input  _11,
  output [1:0] X_
);

  or or_1 (X_[1], _11, _10);
  or or_2 (X_[0], _11, _01);

  // Notes on the sheet:
  //   _10: pull=down
  //   _00: pull=down
  //   _01: pull=down
  //   _11: pull=down
endmodule

module Counter (
);

  wire clock_1_out, clock_2_out, flipflo_1_out_1, flipflo_1_out_2, flipflo_2_out_2, flipflo_3_out_1,
       flipflo_3_out_2, nand_1_out, nand_2_out, nand_3_out, nand_4_out, nand_5_out, nand_6_out, nand_7_out,
       nand_8_out, nand_9_out, nand_10_out, nand_11_out, nand_12_out, nand_13_out, nand_14_out, nand_15_out;

  Clock clock_1 (.out(clock_1_out));
  Clock clock_2 (.out(clock_2_out));
  LED led_1 (.in(flipflo_1_out_2));
  FlipFlo flipflo_1 (.in_1(flipflo_1_out_2), .sync(clock_1_out), .out_1(flipflo_1_out_1), .out_2(flipflo_1_out_2));
  LED led_2 (.in(flipflo_3_out_2));
  FlipFlo flipflo_2 (.in_1(flipflo_2_out_2), .sync(flipflo_3_out_1), .out_2(flipflo_2_out_2));  // open: out_1
  FlipFlo flipflo_3 (.in_1(flipflo_3_out_2), .sync(flipflo_1_out_1), .out_1(flipflo_3_out_1), .out_2(flipflo_3_out_2));
  nand nand_1 (nand_1_out, nand_5_out, clock_2_out);
  nand nand_2 (nand_2_out, clock_2_out, nand_3_out);
  nand nand_3 (nand_3_out, nand_5_out, nand_5_out);
  LED led_3 (.in(flipflo_2_out_2));
  nand nand_4 (nand_4_out, nand_1_out, nand_5_out);
  nand nand_5 (nand_5_out, nand_4_out, nand_2_out);
  nand nand_6 (nand_6_out, nand_10_out, nand_4_out);
  nand nand_7 (nand_7_out, nand_4_out, nand_8_out);
  nand nand_8 (nand_8_out, nand_10_out, nand_10_out);
  nand nand_9 (nand_9_out, nand_6_out, nand_10_out);
  nand nand_10 (nand_10_out, nand_9_out, nand_7_out);
  nand nand_11 (nand_11_out, nand_15_out, nand_15_out);
  nand nand_12 (nand_12_out, nand_15_out, nand_9_out);
  nand nand_13 (nand_13_out, nand_9_out, nand_11_out);
  nand nand_14 (nand_14_out, nand_12_out, nand_15_out);
  nand nand_15 (nand_15_out, nand_14_out, nand_13_out);
endmodule

module FlipFlo (
  input  in_1,
  input  sync,
  output out_1,
  output out_2
);

  wire nand_1_out, nand_2_out, nand_3_out;

  nand nand_1 (nand_1_out, in_1, sync);
  nand nand_2 (nand_2_out, sync, nand_3_out);
  nand nand_3 (nand_3_out, in_1, in_1);
  nand nand_4 (out_1, nand_1_out, out_2);
  nand nand_5 (out_2, out_1, nand_2_out);
endmodule
